// Logisim project 8BitCPU.circ as structural Verilog: 2 circuits, main circuit CPU
module CPU (
  input  RES,
  input  RES_2,
  input  BO,
  input  in_4,
  input  [7:0] in_5,
  output [7:0] out_6
);

  wire AI, and_1_out, AO, BI, CE, CI, clock_1_out, CO, EO, FI, HLT, II, IO, MI, not_1_out, not_2_out, OI,
       or_1_out, RES_t, RI, RO, SU;
  wire [1:0] alu_1_co, FL;
  wire [3:0] bit_extender_1_out, counter_2_q, register_1_q, register_2_q;
  wire [6:0] counter_1_q;
  wire [7:0] register_3_q, register_4_q, register_5_q;

  Clock clock_1 (.out(clock_1_out));
  and and_1 (and_1_out, clock_1_out, not_1_out);
  not not_1 (not_1_out, HLT);
  Button u_RES (.out(RES_t));
  not not_2 (not_2_out, and_1_out);
  Register #(.width(4)) register_1 (.D(bit_extender_1_out), .en(MI), .Q(register_1_q), .clk(and_1_out), .clr(RES_t));
  Bit_Extender #(.out_width(4)) bit_extender_1 (.in(out_6), .out(bit_extender_1_out));
  or or_1 (or_1_out, RI, RO);
  Register register_2 (.D(out_6), .en(II), .Q({counter_1_q[6:3], register_2_q}), .clk(and_1_out), .clr(RES_t));
  Counter #(.width(3), .max('h7)) counter_1 (
    .Q(counter_1_q[2:0]), .clk(not_2_out), .clr(RES_t));  // open: load, D, count, carry
  assign out_6 = IO ? {4'b0000, register_2_q} : 8'bz;  // Controlled_Buffer controlled_buffer_1
  ROM #(.addrWidth(9), .dataWidth(16)) rom_1 (
    .addr({FL, counter_1_q}), .data({HLT, MI, RI, RO, IO, II, AI, AO, EO, SU, BI, OI, CE, CO, CI, FI}),
    .sel(1'b1));
  Pull_Resistor pull_resistor_1 (.node(out_6));
  assign out_6 = CO ? {4'b0000, counter_2_q} : 8'bz;  // Controlled_Buffer controlled_buffer_2
  RAM #(.addrWidth(4)) ram_1 (.addr(register_1_q), .data(out_6), .sel(or_1_out), .clk(and_1_out), .ld(RO), .clr(RES));
  assign out_6 = in_4 ? in_5 : 8'bz;  // Controlled_Buffer controlled_buffer_3
  Register register_3 (.D(out_6), .en(AI), .Q(register_3_q), .clk(and_1_out), .clr(RES_t));
  ALU alu_1 (.B(register_4_q), .A(register_3_q), .R(out_6), .SU(SU), .EO(EO), .CO(alu_1_co[0]), .ZE(alu_1_co[1]));
  Register register_4 (.D(out_6), .en(BI), .Q(register_4_q), .clk(and_1_out), .clr(RES_t));
  Register register_5 (.D(out_6), .en(OI), .Q(register_5_q), .clk(and_1_out), .clr(RES_t));
  Counter #(.width(4), .max('hf)) counter_2 (
    .load(CI), .D(out_6[3:0]), .count(CE), .Q(counter_2_q), .clk(and_1_out), .clr(RES_t));  // open: carry
  assign out_6 = AO ? register_3_q : 8'bz;  // Controlled_Buffer controlled_buffer_4
  assign out_6 = BO ? register_4_q : 8'bz;  // Controlled_Buffer controlled_buffer_5
  Hex_Digit_Display hex_digit_display_1 (.value(register_5_q[7:4]), .dp(1'b0));
  Hex_Digit_Display hex_digit_display_2 (.value(register_5_q[3:0]), .dp(1'b0));
  Register #(.width(2)) register_6 (.D(alu_1_co), .en(FI), .Q(FL), .clk(and_1_out), .clr(RES_2));

  // Notes on the sheet:
  //   contents of rom_1 (hex, n*v repeats v):
  //   4004 1408 6*0 4004 1408 4800 1200 4*0 4004 1408 4800 1020 281 0 0 0 4004 1408 4800 1020 2c1 0 0 0
  //   4004 1408 4800 2100 4*0 4004 1408 a00 5*0 4004 1408 802 5*0 4004 1408 6*0 4004 1408 6*0 4004 1408
  //   6*0 4004 1408 6*0 4004 1408 6*0 4004 1408 6*0 4004 1408 6*0 4004 1408 110 5*0 4004 1408 8000 5*0
  //   4004 1408 6*0 4004 1408 4800 1200 4*0 4004 1408 4800 1020 281 0 0 0 4004 1408 4800 1020 2c1 0 0 0
  //   4004 1408 4800 2100 4*0 4004 1408 a00 5*0 4004 1408 802 5*0 4004 1408 802 5*0 4004 1408 6*0 4004
  //   1408 6*0 4004 1408 6*0 4004 1408 6*0 4004 1408 6*0 4004 1408 6*0 4004 1408 110 5*0 4004 1408 8000
  //   5*0 4004 1408 6*0 4004 1408 4800 1200 4*0 4004 1408 4800 1020 281 0 0 0 4004 1408 4800 1020 2c1 0 0
  //   0 4004 1408 4800 2100 4*0 4004 1408 a00 5*0 4004 1408 802 5*0 4004 1408 6*0 4004 1408 802 5*0 4004
  //   1408 6*0 4004 1408 6*0 4004 1408 6*0 4004 1408 6*0 4004 1408 6*0 4004 1408 110 5*0 4004 1408 8000
  //   5*0 4004 1408 6*0 4004 1408 4800 1200 4*0 4004 1408 4800 1020 281 0 0 0 4004 1408 4800 1020 2c1 0 0
  //   0 4004 1408 4800 2100 4*0 4004 1408 a00 5*0 4004 1408 802 5*0 4004 1408 802 5*0 4004 1408 802 5*0
  //   4004 1408 6*0 4004 1408 6*0 4004 1408 6*0 4004 1408 6*0 4004 1408 6*0 4004 1408 110 5*0 4004 1408
  //   8000
endmodule

module ALU (
  input  SU,
  input  [7:0] B,
  input  [7:0] A,
  input  EO,
  output ZE,
  output [7:0] R,
  output CO
);

  wire [7:0] adder_1_out, xor_1_out;

  assign xor_1_out = {8{SU}} ^ B;  // XOR_Gate xor_1, 8 bits wide
  Adder adder_1 (.a(xor_1_out), .b(A), .out(adder_1_out), .cin(SU), .cout(CO));
  assign R = EO ? adder_1_out : 8'bz;  // Controlled_Buffer controlled_buffer_1
  nor nor_1 (ZE, adder_1_out[0], adder_1_out[1], adder_1_out[2], adder_1_out[3], adder_1_out[4], adder_1_out[5], adder_1_out[6], adder_1_out[7]);
endmodule
