// Logisim project ALU.circ as structural Verilog: 2 circuits, main circuit ALU
module Full_ALU (
  input  [7:0] A,
  input  Sub,
  input  [2:0] Op,
  input  [7:0] B,
  output [7:0] B_2
);

  wire alu_1_cout, alu_2_cout, alu_3_cout, alu_4_cout, alu_5_cout, alu_6_cout, alu_7_cout, alu_8_set;

  ALU alu_1 (
    .A(A[0]), .B(B[0]), .Less(alu_8_set), .Result(B_2[0]), .Sub(Sub), .Cin(Sub), .in_3(Op), .Cout(alu_1_cout));  // open: Set
  ALU alu_2 (
    .A(A[1]), .B(B[1]), .Less(1'b0), .Result(B_2[1]), .Sub(Sub), .Cin(alu_1_cout), .in_3(Op),
    .Cout(alu_2_cout));  // open: Set
  ALU alu_3 (
    .A(A[2]), .B(B[2]), .Less(1'b0), .Result(B_2[2]), .Sub(Sub), .Cin(alu_2_cout), .in_3(Op),
    .Cout(alu_3_cout));  // open: Set
  ALU alu_4 (
    .A(A[3]), .B(B[3]), .Less(1'b0), .Result(B_2[3]), .Sub(Sub), .Cin(alu_3_cout), .in_3(Op),
    .Cout(alu_4_cout));  // open: Set
  ALU alu_5 (
    .A(A[4]), .B(B[4]), .Less(1'b0), .Result(B_2[4]), .Sub(Sub), .Cin(alu_4_cout), .in_3(Op),
    .Cout(alu_5_cout));  // open: Set
  ALU alu_6 (
    .A(A[5]), .B(B[5]), .Less(1'b0), .Result(B_2[5]), .Sub(Sub), .Cin(alu_5_cout), .in_3(Op),
    .Cout(alu_6_cout));  // open: Set
  ALU alu_7 (
    .A(A[6]), .B(B[6]), .Less(1'b0), .Result(B_2[6]), .Sub(Sub), .Cin(alu_6_cout), .in_3(Op),
    .Cout(alu_7_cout));  // open: Set
  ALU alu_8 (
    .A(A[7]), .B(B[7]), .Less(1'b0), .Result(B_2[7]), .Sub(Sub), .Cin(alu_7_cout), .in_3(Op), .Set(alu_8_set));  // open: Cout
endmodule

module ALU (
  input  Sub,
  input  Cin,
  input  [2:0] in_3,
  input  A,
  input  B,
  input  Less,
  output Result,
  output Cout,
  output Set
);

  wire and_1_out, nor_1_out, or_1_out, xor_1_out, xor_2_out;

  and and_1 (and_1_out, A, B);
  or or_1 (or_1_out, A, B);
  xor xor_1 (xor_1_out, A, B);
  nor nor_1 (nor_1_out, A, B);
  Adder #(.width(1)) adder_1 (.a(A), .b(xor_2_out), .out(Set), .cin(Cin), .cout(Cout));
  xor xor_2 (xor_2_out, B, Sub);
  Multiplexer #(.select(3)) multiplexer_1 (
    .in0(and_1_out), .in1(or_1_out), .in2(xor_1_out), .in3(nor_1_out), .in4(Set), .in5(Less), .out(Result),
    .sel(in_3));  // open: in6, in7, en
endmodule
