// Logisim project BenEater8BitCPU(unfinished).circ as structural Verilog: 2 circuits, main circuit CPU
module CPU (
  input  RES,
  input  RES_2,
  input  RES_3,
  input  RES_4,
  input  BO,
  input  RES_5,
  input  RES_6,
  input  in_8,
  input  RES_7,
  input  in_10,
  input  [7:0] in_11,
  output [7:0] out_12,
  output out_13
);

  wire AI, AO, BI, CE, CI, clock_1_out, CO, EO, HLT, II, IO, MI, OI, or_1_out, RI, RO, SU;
  wire [0:0] rom_1_data;
  wire [3:0] counter_2_q, register_1_q, register_2_q_2;
  wire [6:0] register_2_q;
  wire [7:0] register_3_q, register_4_q, register_5_q;

  Clock clock_1 (.out(clock_1_out));
  Register #(.width(4)) register_1 (.D(out_12[3:0]), .en(MI), .Q(register_1_q), .clk(clock_1_out), .clr(RES_2));
  or or_1 (or_1_out, RI, RO);
  Register register_2 (.D(out_12), .en(II), .Q({register_2_q[6:3], register_2_q_2}), .clk(clock_1_out), .clr(RES_6));
  Counter #(.width(3), .max('h7)) counter_1 (
    .Q(register_2_q[2:0]), .clk(clock_1_out), .clr(in_8));  // open: load, D, count, carry
  assign out_12 = IO ? {4'b0000, register_2_q_2} : 8'bz;  // Controlled_Buffer controlled_buffer_1
  ROM #(.addrWidth(7), .dataWidth(16)) rom_1 (
    .addr(register_2_q), .data({HLT, MI, RI, RO, IO, II, AI, AO, EO, SU, BI, OI, CE, CO, CI, rom_1_data[0]}),
    .sel(1'b1));
  assign out_12 = CO ? {4'b0000, counter_2_q} : 8'bz;  // Controlled_Buffer controlled_buffer_2
  RAM #(.addrWidth(4)) ram_1 (
    .addr(register_1_q), .data(out_12), .sel(or_1_out), .clk(clock_1_out), .ld(RO), .clr(RES_4));
  assign out_12 = in_10 ? in_11 : 8'bz;  // Controlled_Buffer controlled_buffer_3
  Register register_3 (.D(out_12), .en(AI), .Q(register_3_q), .clk(clock_1_out), .clr(RES_3));
  ALU alu_1 (.B(register_4_q), .A(register_3_q), .R(out_12), .SU(SU), .EO(EO), .CO(out_13));
  Register register_4 (.D(out_12), .en(BI), .Q(register_4_q), .clk(clock_1_out), .clr(RES_5));
  Register register_5 (.D(out_12), .en(OI), .Q(register_5_q), .clk(clock_1_out), .clr(RES_7));
  Counter #(.width(4), .max('hf)) counter_2 (
    .load(CI), .D(out_12[3:0]), .count(CE), .Q(counter_2_q), .clk(clock_1_out), .clr(RES));  // open: carry
  assign out_12 = AO ? register_3_q : 8'bz;  // Controlled_Buffer controlled_buffer_4
  assign out_12 = BO ? register_4_q : 8'bz;  // Controlled_Buffer controlled_buffer_5
  Hex_Digit_Display hex_digit_display_1 (.value(register_5_q[7:4]), .dp(1'b0));
  Hex_Digit_Display hex_digit_display_2 (.value(register_5_q[3:0]), .dp(1'b0));

  // Notes on the sheet:
  //   contents of rom_1 (hex, n*v repeats v):
  //   4004 1408 6*0 4004 1408 4800 1200 4*0 4004 1408 4800 1020 280 0 0 0 4004 1408 6*0 4004 1408 6*0 4004
  //   1408 6*0 4004 1408 6*0 4004 1408 6*0 4004 1408 6*0 4004 1408 6*0 4004 1408 6*0 4004 1408 6*0 4004
  //   1408 6*0 4004 1408 6*0 4004 1408 110 5*0 4004 1408 802
endmodule

module ALU (
  input  SU,
  input  [7:0] B,
  input  [7:0] A,
  input  EO,
  output [7:0] R,
  output CO
);

  wire [7:0] adder_1_out, xor_1_out;

  assign xor_1_out = {8{SU}} ^ B;  // XOR_Gate xor_1, 8 bits wide
  Adder adder_1 (.a(xor_1_out), .b(A), .out(adder_1_out), .cin(SU), .cout(CO));
  assign R = EO ? adder_1_out : 8'bz;  // Controlled_Buffer controlled_buffer_1
endmodule
