// Logisim project first.circ as structural Verilog: 1 circuit, main circuit main
module main (
);

  wire button_1_out, button_2_out, button_3_out, clock_1_out, not_1_out;
  wire [7:0] adder_1_out, random_1_out, random_2_out;

  Clock clock_1 (.out(clock_1_out));
  LED led_1 (.in(clock_1_out));
  Button button_1 (.out(button_1_out));
  LED led_2 (.in(button_1_out));
  Button button_2 (.out(button_2_out));
  Button button_3 (.out(button_3_out));
  Random random_1 (.clk(clock_1_out), .next(button_2_out), .out(random_1_out));  // open: clr
  Adder adder_1 (.a(random_1_out), .b(random_2_out), .out(adder_1_out));  // open: cin, cout
  Random random_2 (.clk(clock_1_out), .next(button_3_out), .out(random_2_out));  // open: clr
  Register register_1 (.D(adder_1_out), .en(not_1_out), .clk(not_1_out));  // open: Q, clr
  not not_1 (not_1_out, clock_1_out);
endmodule
